# Fritzing sketch CAIXA DE IGNIÇAO (saved by Fritzing 1.0.4)

parts:
  S4 = Toggle Switch spst [package=THT]
  Mod2 = Raspberry Pi Pico
  A2 = LoRa sx1278 module [package=THT]
  S5 = Illuminated Pushbutton
  LED4 = Red LED - Rect 5x2x7mm [package="5x2x7 mm [THT]"]  # not connected
  R2 = Resistor [tolerance=±5% resistance=220 package="1206 [SMD]"]
  LED5 = Yellow LED - Rect 5x2x7mm [package="5x2x7 mm [THT]"]  # not connected
  LED6 = Green LED - Rect 5x2x7mm [package="5x2x7 mm [THT]"]  # not connected
  J3 = Piezo Speaker
  J4 = 2.1mm Barrel Jack with Terminal Block
  LED7 = Yellow LED - Rect 5x2x7mm [package="5x2x7 mm [THT]"]  # not connected
  M1 = 1 chan 5v relay module
  R3 = Resistor [tolerance=±5% resistance=220 package="1206 [SMD]"]  # not connected
  R4 = Resistor [tolerance=±5% resistance=220 package="1206 [SMD]"]  # not connected
  VCC1 = Battery block 9V [internal_resistance=0.1Ω]  # not connected

nets:
  N1: S4.L1, Mod2.pin_40, M1.pin_1
  N2: S4.COM, J4.POS
  N3: Mod2.pin_1, A2.Pin_6
  N4: Mod2.pin_2, A2.Pin_9
  N5: Mod2.pin_3, Mod2.pin_23, Mod2.pin_33, Mod2.pin_42, S5.S-1, J4.NEG, M1.pin_2
  N6: Mod2.pin_14, R2.Pin_0
  N7: Mod2.pin_20, M1.pin_3
  N8: Mod2.pin_27, J3.pin2
  N9: Mod2.pin_36, S5.LED+

custom parts:
  Toggle Switch spst: Toggle Switch single pole single throw
  Raspberry Pi Pico: Raspberry Pi Pico. Based around the RP2040 microcontroller the Pico is a low cost microcontroller device bringing Raspberry Pi quality, cost, and easy of use to the microcontroller space. Jan 2021, Split part in to two versions: tht (this one) and SMD. This one will drill holes for a .1 in header in pcb to allow plugging in the module as well as providing pads to solder the module to the top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
  LoRa sx1278 module: SX1278 Long Range RF Wireless Power Mental Module.
  Red LED - Rect 5x2x7mm: A generic rectangular red LED (~1.8V) 5mm x 2mm x 7mm
  Yellow LED - Rect 5x2x7mm: A generic rectangular yellow LED (~1.8V) 5mm x 2mm x 7mm
  Green LED - Rect 5x2x7mm: A generic rectangular green LED (~1.8V) 5mm x 2mm x 7mm
  1 chan 5v relay module: 1 Channel 5V Relay Module Board Shield with Optocoupler Support High and Low Level Trigger for Arduino.
