# Fritzing sketch ESTAÇAO DE COMANDO (saved by Fritzing 1.0.6)

parts:
  LED2 = Yellow LED - Rect 5x2x7mm [package="5x2x7 mm [THT]"]  # not connected
  LED3 = Green LED - Rect 5x2x7mm [package="5x2x7 mm [THT]"]  # not connected
  R3 = Resistor [tolerance=±5% resistance=220 package="1206 [SMD]"]
  S3 = Toggle Switch spst [package=THT]
  J2 = 2.1mm Barrel Jack with Terminal Block
  S2 = Illuminated Pushbutton
  LED1 = Red LED - Rect 5x2x7mm [package="5x2x7 mm [THT]"]
  S1 = Toggle Switch spst [package=THT]
  Mod1 = Raspberry Pi Pico
  buz1 = Piezo Buzzer
  Buck_Convertor1 = Buck Convertor [part_number=LM2596 package=THT]
  R4 = Resistor [tolerance=±5% resistance=220 package="1206 [SMD]"]
  R5 = Resistor [tolerance=±5% resistance=220 package="1206 [SMD]"]
  M1 = Osoyoo SX1278-ra-02

nets:
  N1: R3.Pin_0, Mod1.pin_16
  N2: S3.L1, Mod1.pin_19
  N3: S3.COM, S2.S-2, LED1.anode, Mod1.pin_3, Mod1.pin_18, Mod1.pin_23, Mod1.pin_28, Mod1.pin_33, Mod1.pin_38, Mod1.pin_42, buz1.pin_2, Buck_Convertor1.Negative_Output, M1.GND
  N4: J2.POS, S1.COM
  N5: J2.NEG, Buck_Convertor1.Negative_Input
  N6: S2.S-1, Mod1.pin_24
  N7: S1.L1, Buck_Convertor1.Positive_Input
  N8: Mod1.pin_1, M1.MOSI
  N9: Mod1.pin_2, M1.NSS
  N10: Mod1.pin_4, M1.SCK
  N11: Mod1.pin_5, M1.MISO
  N12: Mod1.pin_6, M1.RST
  N13: Mod1.pin_14, R5.Pin_0
  N14: Mod1.pin_15, R4.Pin_0
  N15: Mod1.pin_25, buz1.pin_1
  N16: Mod1.pin_36, M1.3.3V
  N17: Mod1.pin_39, Buck_Convertor1.Positive_Output

custom parts:
  Yellow LED - Rect 5x2x7mm: A generic rectangular yellow LED (~1.8V) 5mm x 2mm x 7mm
  Green LED - Rect 5x2x7mm: A generic rectangular green LED (~1.8V) 5mm x 2mm x 7mm
  Toggle Switch spst: Toggle Switch single pole single throw
  Red LED - Rect 5x2x7mm: A generic rectangular red LED (~1.8V) 5mm x 2mm x 7mm
  Raspberry Pi Pico: Raspberry Pi Pico. Based around the RP2040 microcontroller the Pico is a low cost microcontroller device bringing Raspberry Pi quality, cost, and easy of use to the microcontroller space. Jan 2021, Split part in to two versions: tht (this one) and SMD. This one will drill holes for a .1 in header in pcb to allow plugging in the module as well as providing pads to solder the module to the top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
  Piezo Buzzer: Part from https://www.nutsvolts.com/magazine/article/november2012_SmileysWorkshop modified to be .3 in spacing to match the adafruit buzzer 5V breadboard friendly part.
  Buck Convertor: DC to DC buck convertor
  Osoyoo SX1278-ra-02: Osoyoo Long Distance wireless transceiver Uart LoRa Module.
